# Fritzing sketch CAN-BUS-Weichendecoder (saved by Fritzing 0.9.4)
circuit board: 10.7167cm x 7.30796cm
breadboards: 1

parts:
  M1 = Niren can bus module [package=THT]
  Bauteil1 = Arduino Nano (Rev3.0)
  IC1 = ULN2803A [package=THT]
  IC2 = ULN2803A [package=THT]

nets:
  N1: M1.pin1, Bauteil1.5V
  N2: M1.pin2, Bauteil1.GND
  N3: M1.pin3, Bauteil1.D10
  N4: M1.pin4, Bauteil1.D12/MISO
  N5: M1.pin5, Bauteil1.D11/MOSI
  N6: M1.pin6, Bauteil1.D13/SCK
  N7: M1.pin7, Bauteil1.D2
  N8: Bauteil1.D4, IC1.In_6
  N9: Bauteil1.D5, IC1.In_5
  N10: Bauteil1.D6, IC1.In_4
  N11: Bauteil1.D7, IC1.In_3
  N12: Bauteil1.D8, IC1.In_2
  N13: Bauteil1.D9, IC1.In_1
  N14: Bauteil1.A5, IC2.In_4
  N15: Bauteil1.A4, IC2.In_3
  N16: Bauteil1.A3, IC2.In_2
  N17: Bauteil1.A2, IC2.In_1
  N18: Bauteil1.A1, IC1.In_8
  N19: Bauteil1.A0, IC1.In_7

custom parts:
  Niren can bus module: Niren can bus module availabe on ebay and others. Pcb view assumes that you unsolder the 7 pin header and resolder it on the bottom of the module to connect to the pcb. The two jumpers and the can bus connector remain on the top of the board and don't appear in pcb view.
